// Logisim project cpuv2.circ as structural Verilog: 2 circuits, main circuit main
module main (
);

  wire alu_1_output1, clock_1_out, decoder_1_out0, decoder_1_out1, decoder_1_out2, decoder_1_out3,
       decoder_1_out4, decoder_1_out5, decoder_1_out6, decoder_1_out7, decoder_1_out8, decoder_1_out9,
       decoder_1_out10, decoder_1_out11, decoder_1_out12, decoder_1_out13, decoder_1_out14, decoder_1_out15,
       decoder_1_out16, decoder_1_out17, decoder_1_out18, decoder_1_out19, decoder_2_out0, decoder_2_out3,
       decoder_2_out4, decoder_2_out11, decoder_2_out14, decoder_2_out22, not_1_out, not_2_out, or_1_out;
  wire [15:0] adder_1_out, controlled_buffer_1_out, counter_1_q, multiplexer_1_out, multiplexer_2_out,
       multiplexer_3_out, multiplexer_4_out, multiplexer_5_out, ram_1_dout, reg0_q, reg1_q, reg2_q, reg3_q,
       reg4_q, reg5_q, reg6_q, reg7_q, reg8_q, reg9_q, reg10_q, reg11_q, reg12_q, reg13_q, reg14_q, reg15_q,
       reg16_q, reg17_q, reg18_q, reg19_q, rom_1_p2, rom_1_p3, rom_1_p4, rom_1_p5;

  Clock clock_1 (.out(clock_1_out));
  Adder #(.width(16)) adder_1 (.a(counter_1_q), .b(16'h4), .out(adder_1_out));  // open: cin, cout
  Counter #(.max('hffff), .width(16)) counter_1 (
    .clr(decoder_2_out14), .load(clock_1_out), .clk(clock_1_out), .D(multiplexer_1_out), .Q(counter_1_q));  // open: up, count, carry
  Multiplexer #(.width(16)) multiplexer_1 (
    .in0(adder_1_out), .in1(rom_1_p3), .out(multiplexer_1_out), .sel(alu_1_output1));
  // ROM #(.addrWidth(16), .dataWidth(16), .line("quad")) rom_1: pin names not known; wires that end beside it: counter_1_q, rom_1_p2, rom_1_p3, rom_1_p4, rom_1_p5
  Decoder #(.select(5)) decoder_1 (
    .out0(decoder_1_out0), .out1(decoder_1_out1), .out2(decoder_1_out2), .out3(decoder_1_out3),
    .out4(decoder_1_out4), .out5(decoder_1_out5), .out6(decoder_1_out6), .out7(decoder_1_out7),
    .out8(decoder_1_out8), .out9(decoder_1_out9), .out10(decoder_1_out10), .out11(decoder_1_out11),
    .out12(decoder_1_out12), .out13(decoder_1_out13), .out14(decoder_1_out14), .out15(decoder_1_out15),
    .out16(decoder_1_out16), .out17(decoder_1_out17), .out18(decoder_1_out18), .out19(decoder_1_out19),
    .sel(rom_1_p5[4:0]));  // open: out20, out21, out22, out23, out24, out25, out26, out27, out28, out29, out30, out31, en
  Decoder #(.select(5)) decoder_2 (
    .out0(decoder_2_out0), .out3(decoder_2_out3), .out4(decoder_2_out4), .out11(decoder_2_out11),
    .out14(decoder_2_out14), .out22(decoder_2_out22), .sel(rom_1_p2[4:0]));  // open: out1, out2, out5, out6, out7, out8, out9, out10, out12, out13, out15, out16, out17, out18, out19, out20, out21, out23, out24, out25, out26, out27, out28, out29, out30, out31, en
  assign controlled_buffer_1_out = decoder_2_out0 ? rom_1_p3 : 16'bz;  // Controlled_Buffer controlled_buffer_1
  Register #(.width(16)) reg0 (
    .D(controlled_buffer_1_out), .en(decoder_1_out0), .clk(clock_1_out), .Q(reg0_q));  // open: clr
  Register #(.width(16)) reg1 (
    .D(controlled_buffer_1_out), .en(decoder_1_out1), .clk(clock_1_out), .Q(reg1_q));  // open: clr
  Register #(.width(16)) reg2 (
    .D(controlled_buffer_1_out), .en(decoder_1_out2), .clk(clock_1_out), .Q(reg2_q));  // open: clr
  Register #(.width(16)) reg3 (
    .D(controlled_buffer_1_out), .en(decoder_1_out3), .clk(clock_1_out), .Q(reg3_q));  // open: clr
  Register #(.width(16)) reg4 (
    .D(controlled_buffer_1_out), .en(decoder_1_out4), .clk(clock_1_out), .Q(reg4_q));  // open: clr
  Register #(.width(16)) reg5 (
    .D(controlled_buffer_1_out), .en(decoder_1_out5), .clk(clock_1_out), .Q(reg5_q));  // open: clr
  Register #(.width(16)) reg6 (
    .D(controlled_buffer_1_out), .en(decoder_1_out6), .clk(clock_1_out), .Q(reg6_q));  // open: clr
  Register #(.width(16)) reg7 (
    .D(controlled_buffer_1_out), .en(decoder_1_out7), .clk(clock_1_out), .Q(reg7_q));  // open: clr
  Register #(.width(16)) reg8 (
    .D(controlled_buffer_1_out), .en(decoder_1_out8), .clk(clock_1_out), .Q(reg8_q));  // open: clr
  Register #(.width(16)) reg9 (
    .D(controlled_buffer_1_out), .en(decoder_1_out9), .clk(clock_1_out), .Q(reg9_q));  // open: clr
  Register #(.width(16)) reg10 (
    .D(controlled_buffer_1_out), .en(decoder_1_out10), .clk(clock_1_out), .Q(reg10_q));  // open: clr
  Register #(.width(16)) reg11 (
    .D(controlled_buffer_1_out), .en(decoder_1_out11), .clk(clock_1_out), .Q(reg11_q));  // open: clr
  Register #(.width(16)) reg12 (
    .D(controlled_buffer_1_out), .en(decoder_1_out12), .clk(clock_1_out), .Q(reg12_q));  // open: clr
  Register #(.width(16)) reg13 (
    .D(controlled_buffer_1_out), .en(decoder_1_out13), .clk(clock_1_out), .Q(reg13_q));  // open: clr
  Register #(.width(16)) reg14 (
    .D(controlled_buffer_1_out), .en(decoder_1_out14), .clk(clock_1_out), .Q(reg14_q));  // open: clr
  Register #(.width(16)) reg15 (
    .D(controlled_buffer_1_out), .en(decoder_1_out15), .clk(clock_1_out), .Q(reg15_q));  // open: clr
  Register #(.width(16)) reg16 (
    .D(controlled_buffer_1_out), .en(decoder_1_out16), .clk(clock_1_out), .Q(reg16_q));  // open: clr
  Register #(.width(16)) reg17 (
    .D(controlled_buffer_1_out), .en(decoder_1_out17), .clk(clock_1_out), .Q(reg17_q));  // open: clr
  Register #(.width(16)) reg18 (
    .D(controlled_buffer_1_out), .en(decoder_1_out18), .clk(clock_1_out), .Q(reg18_q));  // open: clr
  Register #(.width(16)) reg19 (
    .D(controlled_buffer_1_out), .en(decoder_1_out19), .clk(clock_1_out), .Q(reg19_q));  // open: clr
  RAM #(.addrWidth(16), .dataWidth(16)) ram_1 (
    .addr(multiplexer_5_out), .we(decoder_2_out11), .oe(1'b1), .clk(clock_1_out), .din(multiplexer_3_out),
    .dout(ram_1_dout));
  not not_1 (not_1_out, decoder_2_out3);
  assign controlled_buffer_1_out = decoder_2_out22 ? ram_1_dout : 16'bz;  // Controlled_Buffer controlled_buffer_2
  Multiplexer #(.width(16)) multiplexer_2 (
    .in0(rom_1_p3), .in1(multiplexer_3_out), .out(multiplexer_2_out), .sel(not_1_out));
  Multiplexer #(.select(5), .width(16)) multiplexer_3 (
    .in0(reg0_q), .in1(reg1_q), .in2(reg2_q), .in3(reg3_q), .in4(reg4_q), .in5(reg5_q), .in6(reg6_q),
    .in7(reg7_q), .in8(reg8_q), .in9(reg9_q), .in10(reg10_q), .in11(reg11_q), .in12(reg12_q), .in13(reg13_q),
    .in14(reg14_q), .in15(reg15_q), .in16(reg16_q), .in17(reg17_q), .in18(reg18_q), .in19(reg19_q),
    .out(multiplexer_3_out), .sel(rom_1_p3[4:0]));  // open: in20, in21, in22, in23, in24, in25, in26, in27, in28, in29, in30, in31
  or or_1 (or_1_out, decoder_2_out11, decoder_2_out4);
  not not_2 (not_2_out, or_1_out);
  Multiplexer #(.width(16)) multiplexer_4 (
    .in0(rom_1_p4), .in1(multiplexer_5_out), .out(multiplexer_4_out), .sel(not_2_out));
  Multiplexer #(.select(5), .width(16)) multiplexer_5 (
    .in0(reg0_q), .in1(reg1_q), .in2(reg2_q), .in3(reg3_q), .in4(reg4_q), .in5(reg5_q), .in6(reg6_q),
    .in7(reg7_q), .in8(reg8_q), .in9(reg9_q), .in10(reg10_q), .in11(reg11_q), .in12(reg12_q), .in13(reg13_q),
    .in14(reg14_q), .in15(reg15_q), .in16(reg16_q), .in17(reg17_q), .in18(reg18_q), .in19(reg19_q),
    .out(multiplexer_5_out), .sel(rom_1_p4[4:0]));  // open: in20, in21, in22, in23, in24, in25, in26, in27, in28, in29, in30, in31
  alu alu_1 (
    .Input0(multiplexer_2_out), .Input1(multiplexer_4_out), .Instruction(rom_1_p2),
    .Output0(controlled_buffer_1_out), .Output1(alu_1_output1));
endmodule

module alu (
  input  [15:0] Instruction,
  input  [15:0] Input0,
  input  [15:0] Input1,
  output [15:0] Output0,
  output Output1
);

  wire decoder_1_out1, decoder_1_out2, decoder_1_out3, decoder_1_out4, decoder_1_out5, decoder_1_out6,
       decoder_1_out7, decoder_1_out8, decoder_1_out9, decoder_1_out10, or_1_out;
  wire [15:0] adder_1_out, and_16_out, divider_1_out, multiplier_1_out, nor_16_out, or_17_out,
       subtractor_1_out;

  assign Output0 = decoder_1_out1 ? Input0 : 16'bz;  // Controlled_Buffer controlled_buffer_1
  Decoder #(.enable("false"), .select(5)) decoder_1 (
    .out1(decoder_1_out1), .out2(decoder_1_out2), .out3(decoder_1_out3), .out4(decoder_1_out4),
    .out5(decoder_1_out5), .out6(decoder_1_out6), .out7(decoder_1_out7), .out8(decoder_1_out8),
    .out9(decoder_1_out9), .out10(decoder_1_out10), .out15(Output1), .sel(Instruction[4:0]));  // open: out0, out11, out12, out13, out14, out16, out17, out18, out19, out20, out21, out22, out23, out24, out25, out26, out27, out28, out29, out30, out31
  or or_1 (or_1_out, decoder_1_out2, decoder_1_out3, decoder_1_out4);
  assign Output0 = or_1_out ? adder_1_out : 16'bz;  // Controlled_Buffer controlled_buffer_2
  Adder #(.width(16)) adder_1 (.a(Input0), .b(Input1), .out(adder_1_out));  // open: cin, cout
  assign Output0 = decoder_1_out5 ? subtractor_1_out : 16'bz;  // Controlled_Buffer controlled_buffer_3
  Subtractor #(.width(16)) subtractor_1 (.a(Input0), .b(Input1), .out(subtractor_1_out));  // open: bin, bout
  assign Output0 = decoder_1_out6 ? multiplier_1_out : 16'bz;  // Controlled_Buffer controlled_buffer_4
  Multiplier #(.width(16)) multiplier_1 (.a(Input0), .b(Input1), .out(multiplier_1_out));  // open: cin, cout
  assign Output0 = decoder_1_out7 ? divider_1_out : 16'bz;  // Controlled_Buffer controlled_buffer_5
  Divider #(.width(16)) divider_1 (.a(Input0), .b(Input1), .out(divider_1_out));  // open: upper, rem
  assign Output0 = decoder_1_out8 ? and_16_out : 16'bz;  // Controlled_Buffer controlled_buffer_6
  and and_1 (and_16_out[15], Input1[15], Input0[15]);
  and and_2 (and_16_out[14], Input1[14], Input0[14]);
  and and_3 (and_16_out[13], Input1[13], Input0[13]);
  and and_4 (and_16_out[12], Input1[12], Input0[12]);
  and and_5 (and_16_out[11], Input1[11], Input0[11]);
  and and_6 (and_16_out[10], Input1[10], Input0[10]);
  and and_7 (and_16_out[9], Input1[9], Input0[9]);
  and and_8 (and_16_out[8], Input1[8], Input0[8]);
  and and_9 (and_16_out[7], Input1[7], Input0[7]);
  and and_10 (and_16_out[6], Input1[6], Input0[6]);
  and and_11 (and_16_out[5], Input1[5], Input0[5]);
  and and_12 (and_16_out[4], Input1[4], Input0[4]);
  and and_13 (and_16_out[3], Input1[3], Input0[3]);
  and and_14 (and_16_out[2], Input1[2], Input0[2]);
  and and_15 (and_16_out[1], Input1[1], Input0[1]);
  and and_16 (and_16_out[0], Input1[0], Input0[0]);
  assign Output0 = decoder_1_out9 ? or_17_out : 16'bz;  // Controlled_Buffer controlled_buffer_7
  or or_2 (or_17_out[15], Input1[15], Input0[15]);
  or or_3 (or_17_out[14], Input1[14], Input0[14]);
  or or_4 (or_17_out[13], Input1[13], Input0[13]);
  or or_5 (or_17_out[12], Input1[12], Input0[12]);
  or or_6 (or_17_out[11], Input1[11], Input0[11]);
  or or_7 (or_17_out[10], Input1[10], Input0[10]);
  or or_8 (or_17_out[9], Input1[9], Input0[9]);
  or or_9 (or_17_out[8], Input1[8], Input0[8]);
  or or_10 (or_17_out[7], Input1[7], Input0[7]);
  or or_11 (or_17_out[6], Input1[6], Input0[6]);
  or or_12 (or_17_out[5], Input1[5], Input0[5]);
  or or_13 (or_17_out[4], Input1[4], Input0[4]);
  or or_14 (or_17_out[3], Input1[3], Input0[3]);
  or or_15 (or_17_out[2], Input1[2], Input0[2]);
  or or_16 (or_17_out[1], Input1[1], Input0[1]);
  or or_17 (or_17_out[0], Input1[0], Input0[0]);
  assign Output0 = decoder_1_out10 ? nor_16_out : 16'bz;  // Controlled_Buffer controlled_buffer_8
  nor nor_1 (nor_16_out[15], Input1[15], Input0[15]);
  nor nor_2 (nor_16_out[14], Input1[14], Input0[14]);
  nor nor_3 (nor_16_out[13], Input1[13], Input0[13]);
  nor nor_4 (nor_16_out[12], Input1[12], Input0[12]);
  nor nor_5 (nor_16_out[11], Input1[11], Input0[11]);
  nor nor_6 (nor_16_out[10], Input1[10], Input0[10]);
  nor nor_7 (nor_16_out[9], Input1[9], Input0[9]);
  nor nor_8 (nor_16_out[8], Input1[8], Input0[8]);
  nor nor_9 (nor_16_out[7], Input1[7], Input0[7]);
  nor nor_10 (nor_16_out[6], Input1[6], Input0[6]);
  nor nor_11 (nor_16_out[5], Input1[5], Input0[5]);
  nor nor_12 (nor_16_out[4], Input1[4], Input0[4]);
  nor nor_13 (nor_16_out[3], Input1[3], Input0[3]);
  nor nor_14 (nor_16_out[2], Input1[2], Input0[2]);
  nor nor_15 (nor_16_out[1], Input1[1], Input0[1]);
  nor nor_16 (nor_16_out[0], Input1[0], Input0[0]);
endmodule
